# Fritzing sketch sensors (saved by Fritzing 0.9.3b)
breadboards: 1

parts:
  T4 = LED - 3mm [color="Red (633nm)" package="3 mm [THT]"]
  R4 = LED - 3mm [color="Red (633nm)" package="3 mm [THT]"]
  T3 = LED - 3mm [color="Red (633nm)" package="3 mm [THT]"]
  R3 = LED - 3mm [color="Red (633nm)" package="3 mm [THT]"]
  R5 = LED - 3mm [color="Red (633nm)" package="3 mm [THT]"]
  T5 = LED - 3mm [color="Red (633nm)" package="3 mm [THT]"]
  R6 = LED - 3mm [color="Red (633nm)" package="3 mm [THT]"]
  T6 = LED - 3mm [color="Red (633nm)" package="3 mm [THT]"]
  R2 = LED - 3mm [color="Red (633nm)" package="3 mm [THT]"]
  T2 = LED - 3mm [color="Red (633nm)" package="3 mm [THT]"]
  R1 = LED - 3mm [color="Red (633nm)" package="3 mm [THT]"]
  T1 = LED - 3mm [color="Red (633nm)" package="3 mm [THT]"]
  R7 = LED - 3mm [color="Red (633nm)" package="3 mm [THT]"]
  T7 = LED - 3mm [color="Red (633nm)" package="3 mm [THT]"]
  R8 = LED - 3mm [color="Red (633nm)" package="3 mm [THT]"]
  T8 = LED - 3mm [color="Red (633nm)" package="3 mm [THT]"]
  R0 = LED - 3mm [color="Red (633nm)" package="3 mm [THT]"]
  T0 = LED - 3mm [color="Red (633nm)" package="3 mm [THT]"]

nets:
  N1: T4.cathode, T3.cathode, T5.cathode, T6.cathode, T2.cathode
  N2: T4.anode, T3.anode, T5.anode, T6.anode, T2.anode, T1.anode, T7.anode, T8.anode, T0.anode
  N3: R4.cathode, R3.cathode, R5.cathode, R6.cathode, R2.cathode, R1.cathode, R7.cathode, R8.cathode, R0.cathode
  N4: T1.cathode, T7.cathode, T8.cathode, T0.cathode
